# Fritzing sketch elektroniczny_potencjometr (saved by Fritzing 0.9.3b)

parts:
  U1 = Module 4 Relais 5V [package="Module 4 Relais 5V"]
  U2 = ESP8266 NodeMCU LoLin module
  Mod1 = generic-ac-power-supply [package=THT]
  Power_plug1 = Power plug
  Part1 = Current Sensor 5A
  R1 = Resistor [tolerance=±5% resistance=250k package="0402 [SMD]"]
  R2 = Resistor [tolerance=±5% resistance=125k package="0402 [SMD]"]
  R3 = Resistor [tolerance=±5% resistance=62.5k package="0402 [SMD]"]
  R4 = Resistor [tolerance=±5% resistance=31.25k package="0402 [SMD]"]
  A1 = PWM DC Motor Speed Controller
  Power_plug2 = Power plug

nets:
  VCC: U1.VCC, U2.Vin, Mod1.pin3#2
  GND: U1.GND, U2.GND, Mod1.pin3#3, Part1.GND
  N1: U1.IN1, U2.D5
  N2: U1.IN2, U2.D6
  N3: U1.IN3, U2.D7
  N4: U1.IN4, U2.D2
  N5: U1.K2-NF, U1.K1-Com, R4.Pin_0
  N6: U1.K3-NF, U1.K2-Com, R3.Pin_0
  N7: U1.K4-NF, U1.K3-Com, Mod1.pin1, Power_plug1.GND, R2.Pin_0, A1.pin1
  N8: U1.K4-Com, R1.Pin_0
  N9: U1.K1-NO, R4.Pin_1
  N10: U1.K2-NO, R3.Pin_1
  N11: U1.K3-NO, R2.Pin_1
  N12: U1.K4-NO, R1.Pin_1
  3V3: U2.3V3, Part1.VCC
  N13: U2.A0, Part1.2, Part1.OUT, A1.pin4, Power_plug2.GND
  N14: Mod1.pin2, Power_plug1.VCC, A1.pin2
  N15: Part1.1, A1.pin3, Power_plug2.VCC

notes:
  230V AC
  AD-DC 5V
  ACS712
  ESP-12
  POTENTIOMETER
  (could be removed)
  INPUT
  OUTPUT
  OUPUT

custom parts:
  Module 4 Relais 5V: Module 4 Relais 5V 4x SPD-06VDC-SD-C
  ESP8266 NodeMCU LoLin module: ESP8266 based NodeMCU
  generic-ac-power-supply: Generic ac power supply module. Use as is, or customize the svgs to fit your particular device (as they are all different.) Provides AC input and single DC output. PCB is generic and will need modifications if you intend to do a pcb mount.
  PWM DC Motor Speed Controller: AZDelivery Motor Speed Controller PWM Module DC Motor Speed Switch.
